# Fritzing sketch 3sensors (saved by Fritzing 0.9.3b)
breadboards: 1

parts:
  Raspberry_Pi_1 = Raspberry Pi 3 [part_number=RPI-3-V1.2]
  LED1 = smd LED [color="Red (633nm)" package="1206 [SMD]"]
  LED2 = smd LED [color="Yellow (595nm)" package="0805 [SMD]"]
  LED3 = smd LED [color="Green (570nm)" package="0805 [SMD]"]
  IR1 = TSOP312.., 314.. [package=THT]
  R1 = Resistor [tolerance=±5% resistance=220 package=THT]
  R2 = Resistor [tolerance=±5% resistance=220 package=THT]
  R3 = Resistor [tolerance=±5% resistance=220 package=THT]
  Q1 = PNP-Transistor [package="TO92 [THT]"]
  J1 = Piezo Speaker

nets:
  N1: Raspberry_Pi_1.3v3, IR1.Data
  N2: Raspberry_Pi_1.GND, LED1.cathode, LED2.cathode, LED3.cathode, IR1.Vs, Q1.E
  N3: Raspberry_Pi_1.GIPO13, R3.Pin_1
  N4: Raspberry_Pi_1.GIPO19, R2.Pin_1
  N5: Raspberry_Pi_1.GIPO26, R1.Pin_1
  N6: Raspberry_Pi_1.GIPO21, Q1.C
  N7: Raspberry_Pi_1.GIPO18, IR1.GND
  N8: Raspberry_Pi_1.5V, J1.pin2
  N9: LED1.anode, R2.Pin_0
  N10: LED2.anode, R3.Pin_0
  N11: LED3.anode, R1.Pin_0
  N12: Q1.B, J1.pin1

notes:
  tilt sensor
